// Logisim project cpuproj.circ as structural Verilog: 1 circuit, main circuit main
module main (
  input  [1:0] ReadReg1,
  input  [1:0] WriteReg,
  input  WriteEnable,
  input  [1:0] ReadReg2,
  input  [7:0] in_5,
  output [7:0] RegData1,
  output [7:0] ReadDataM,
  output [7:0] RegData2,
  output [7:0] RegDataW
);

  wire and_1_out, and_2_out, and_3_out, and_4_out, decoder_1_out0, decoder_1_out1, decoder_1_out2,
       decoder_1_out3, TheClock_out;
  wire [7:0] adder_1_out, multiplexer_3_out, multiplexer_4_out, PC_q, subtractor_1_out, X0_q, X1_q, X2_q,
       X3_q;

  Clock TheClock (.out(TheClock_out));
  Decoder #(.select(2)) decoder_1 (
    .out0(decoder_1_out0), .out1(decoder_1_out1), .out2(decoder_1_out2), .out3(decoder_1_out3), .sel(WriteReg));  // open: en
  Register X0 (.D(ReadDataM), .en(and_1_out), .clk(TheClock_out), .Q(X0_q));  // open: clr
  and and_1 (and_1_out, WriteEnable, decoder_1_out0);
  Register X1 (.D(ReadDataM), .en(and_2_out), .clk(TheClock_out), .Q(X1_q));  // open: clr
  and and_2 (and_2_out, WriteEnable, decoder_1_out1);
  Register X2 (.D(ReadDataM), .en(and_3_out), .clk(TheClock_out), .Q(X2_q));  // open: clr
  and and_3 (and_3_out, WriteEnable, decoder_1_out2);
  Register X3 (.D(ReadDataM), .en(and_4_out), .clk(TheClock_out), .Q(X3_q));  // open: clr
  and and_4 (and_4_out, WriteEnable, decoder_1_out3);
  Multiplexer #(.select(2), .width(8)) multiplexer_1 (
    .in0(X0_q), .in1(X1_q), .in2(X2_q), .in3(X3_q), .out(RegData1), .sel(ReadReg1));
  Multiplexer #(.select(2), .width(8)) multiplexer_2 (
    .in0(X0_q), .in1(X1_q), .in2(X2_q), .in3(X3_q), .out(RegData2), .sel(ReadReg2));
  Multiplexer #(.width(8)) multiplexer_3 (.in0(RegData2), .in1(in_5), .out(multiplexer_3_out), .sel(1'b1));
  Adder adder_1 (.a(RegData1), .b(multiplexer_3_out), .out(adder_1_out));  // open: cin, cout
  Subtractor subtractor_1 (.a(RegData1), .b(multiplexer_3_out), .out(subtractor_1_out));  // open: bin, bout
  Multiplexer #(.width(8)) multiplexer_4 (
    .in0(adder_1_out), .in1(subtractor_1_out), .out(multiplexer_4_out), .sel(1'b0));
  Register PC (.D(multiplexer_4_out), .en(1'b1), .clk(TheClock_out), .Q(PC_q));  // open: clr
  RAM ram_1 (.addr(PC_q), .we(1'b0), .oe(1'b1), .clk(TheClock_out), .din(RegData2), .dout(ReadDataM));

  assign RegDataW = ReadDataM;

  // Notes on the sheet:
  //   Register File
  //   ts wirte for the imm
  //   ALU
  //   write enable has to be on to write into memeory
  //   Data Memory
  //   I pledge my honor that I have abided by the Stevens Honor System -Alvaro Izquierdo
  //   this will calc the offset right now its just offsetting by 1
endmodule
